# Fritzing sketch two_LED_with_Button (saved by Fritzing 0.9.10b)
breadboards: 1

parts:
  Part1 = Arduino Mega 2560 (Rev3)
  LED1 = LED - 5mm [color="Red (633nm)" current=0.030 package="5 mm [THT]"]
  R1 = Resistor [tolerance=±5% power=0.25 resistance=100 package=THT]
  LED2 = LED - 5mm [color="Blue (525nm)" current=0.030 package="5 mm [THT]"]
  R2 = Resistor [tolerance=±5% power=0.25 resistance=100 package=THT]
  S1 = Pushbutton [package="[THT]"]

nets:
  N1: Part1.GND, R1.Pin_0, R2.Pin_0, S1.Pin_1, S1.Pin_2
  N2: Part1.D13_PWM, LED1.anode
  N3: Part1.D12_PWM, LED2.anode
  N4: Part1.D2_PWM, S1.Pin_3, S1.Pin_4
  N5: LED1.cathode, R1.Pin_1
  N6: LED2.cathode, R2.Pin_1

// code stored in the sketch: one_LED.ino
void setup() {
  pinMode(LED_BUILTIN, INPUT);


}


void loop() {
  digitalWrite(LED_BUILTIN, HIGH);
  delay(500);
  digitalWrite(LED_BUILTIN, LOW);
  delay(500);


}


